# Fritzing sketch BreadBoard_Lab01 (saved by Fritzing 0.9.3b)
breadboards: 1

parts:
  S1 = SWITCH-MOMENTARY-2 [package=tactile-switch-1101ne]
  R1 = Resistor [tolerance=±5% resistance=1k package=THT]
  Part1 = Arduino Mega 2560 (Rev3) [part_number="Asset Tracking by VRU Mecha & RoBot 62"]
  U1 = LCD-16X2 [package=lcd-16x2_noholes]  # not connected
  JP1 = Header 4 [package=screwterminal-3.5mm-4_lock]
  Part2 = SO-24x [chip_label=SO-24x package=SO(x)]  # not connected
  R2 = Resistor [tolerance=±5% resistance=1k package=THT]
  S2 = SWITCH-MOMENTARY-2 [package=tactile-switch-1101ne]

nets:
  N1: S1.1, Part1.5V, JP1.3, S2.1
  N2: S1.2, R1.Pin_1, Part1.D2_PWM, R2.Pin_1, S2.2
  N3: R1.Pin_0, Part1.GND, JP1.4, R2.Pin_0
  N4: Part1.D21/SCL, JP1.1
  N5: Part1.D20/SDA, Part1.SDA, JP1.2

notes:
  SCL
  SDA
  5 V
  GND
